# Fritzing sketch motor_controller (saved by Fritzing 1.0.4)

parts:
  M2 = motor driver shz-mdbl-010 [package=THT]
  M3 = DC Motor [voltage_(max)=6V voltage_(min)=3V]
  A1 = Raspberry Pi Pico

nets:
  N1: M2.pin_3, M3.pin_2
  N2: M2.pin_4, M3.pin_1
  N3: M2.pin_5, A1.pin_40
  N4: M2.pin_6, A1.pin_18, A1.pin_33
  N5: M2.pin_7, A1.pin_21
  N6: M2.pin_8, A1.pin_22

custom parts:
  motor driver shz-mdbl-010: Motor drive module is ideal for use in battery-powered smart car, toy cars, robots. Supply voltage 2V ~ 10V, can drive two DC motors or a 4-wire 2-phase stepper motors ,can achieve forward rotation or reverse rotation, it is possible to adjust the rotation speed. Each can provide continuous current of 1.5A, peak current up to 2.5A, thermal protection and can be automatically restored.
  Raspberry Pi Pico: Raspberry Pi Pico. Based around the RP2040 microcontroller the Pico is a low cost microcontroller device bringing Raspberry Pi quality, cost, and easy of use to the microcontroller space. Jan 2021, Split part in to two versions: tht (this one) and SMD. This one will drill holes for a .1 in header in pcb to allow plugging in the module as well as providing pads to solder the module to the top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
