# Fritzing sketch overall (saved by Fritzing 1.0.4)

parts:
  Q1 = Basic FET P-Channel [package="TO220 [THT]"]
  BAT1 = BC9VPC [package=bc9vpc]
  S1 = Toggle Switch [package=THT]
  M2 = DC Motor [voltage_(max)=6V voltage_(min)=3V]
  M3 = DC Motor [voltage_(max)=6V voltage_(min)=3V]
  A1 = Raspberry Pi Pico
  M1 = motor driver shz-mdbl-010 [package=THT]
  LED1 = RGB LED (com. anode, rbg) [color="Red (633nm)" current=0.030A package="5 mm [THT]"]
  R1 = Photocell (LDR) [power=0.25W dark_resistance_@0.01lx=300kΩ light_resistance_@100lx=400Ω luminance=10lx package=THT]
  R2 = Resistor [tolerance=±5% resistance=10k package="0402 [SMD]"]
  LED2 = LED - 5mm [color="Red (633nm)" current=0.030A package="5 mm [THT]"]

nets:
  N1: Q1.gate, S1.COM
  N2: Q1.drain, BAT1.V-, A1.pin_8, A1.pin_23, A1.pin_28, A1.pin_33, A1.pin_38, M1.pin_6, LED1.blue_cathode, R2.Pin_0, LED2.cathode
  N3: Q1.source, A1.pin_39, M1.pin_5
  N4: BAT1.V+, S1.L1
  N5: M2.pin_1, M1.pin_4
  N6: M2.pin_2, M1.pin_3
  N7: M3.pin_1, M1.pin_1
  N8: M3.pin_2, M1.pin_2
  N9: A1.pin_14, M1.pin_10
  N10: A1.pin_15, M1.pin_9
  N11: A1.pin_16, M1.pin_8
  N12: A1.pin_17, M1.pin_7
  N13: A1.pin_21, LED2.anode
  N14: A1.pin_26, LED1.red_cathode
  N15: A1.pin_27, LED1.common_anode
  N16: A1.pin_29, LED1.green_cathode
  N17: A1.pin_34, R1.pin_1
  N18: A1.pin_36, R1.pin_0

notes:
  Power Switch
  Motor Controller (H Bridge)
  Voltage
  Regulator
  DC Motor
  RGB LED
  Laser
  Photoresistor

custom parts:
  Raspberry Pi Pico: Raspberry Pi Pico. Based around the RP2040 microcontroller the Pico is a low cost microcontroller device bringing Raspberry Pi quality, cost, and easy of use to the microcontroller space. Jan 2021, Split part in to two versions: tht (this one) and SMD. This one will drill holes for a .1 in header in pcb to allow plugging in the module as well as providing pads to solder the module to the top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
  motor driver shz-mdbl-010: Motor drive module is ideal for use in battery-powered smart car, toy cars, robots. Supply voltage 2V ~ 10V, can drive two DC motors or a 4-wire 2-phase stepper motors ,can achieve forward rotation or reverse rotation, it is possible to adjust the rotation speed. Each can provide continuous current of 1.5A, peak current up to 2.5A, thermal protection and can be automatically restored.
