# Fritzing sketch simple_led2 (saved by Fritzing 1.0.4)

parts:
  A1 = Raspberry Pi Pico
  LED1 = LED - 5mm [color="Blue (470nm)" current=0.030A package="5 mm [THT]"]

nets:
  N1: A1.pin_21, LED1.anode
  N2: A1.pin_28, A1.pin_33, LED1.cathode

custom parts:
  Raspberry Pi Pico: Raspberry Pi Pico. Based around the RP2040 microcontroller the Pico is a low cost microcontroller device bringing Raspberry Pi quality, cost, and easy of use to the microcontroller space. Jan 2021, Split part in to two versions: tht (this one) and SMD. This one will drill holes for a .1 in header in pcb to allow plugging in the module as well as providing pads to solder the module to the top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
