# Fritzing sketch simple_motor (saved by Fritzing 1.0.4)

parts:
  M1 = DC Motor [voltage_(max)=6V voltage_(min)=3V]
  A1 = Raspberry Pi Pico

nets:
  N1: M1.pin_1, A1.pin_33, A1.pin_38
  N2: M1.pin_2, A1.pin_40

custom parts:
  Raspberry Pi Pico: Raspberry Pi Pico. Based around the RP2040 microcontroller the Pico is a low cost microcontroller device bringing Raspberry Pi quality, cost, and easy of use to the microcontroller space. Jan 2021, Split part in to two versions: tht (this one) and SMD. This one will drill holes for a .1 in header in pcb to allow plugging in the module as well as providing pads to solder the module to the top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
